// Logisim project 4 bit.circ as structural Verilog: 1 circuit, main circuit main
module main (
  input  in_1,
  input  in_2,
  input  in_3,
  input  in_4,
  input  in_5,
  input  in_6,
  input  in_7,
  input  in_8,
  input  in_9
);

  wire adder_1_cout, adder_2_cout, adder_3_cout, adder_4_cout;
  wire [7:0] adder_1_out, adder_2_out, adder_3_out, adder_4_out, xor_1_out, xor_2_out, xor_3_out, xor_4_out;
  wire [7:1] undriven, undriven_2, undriven_3, undriven_4;

  xor xor_1 (xor_1_out[0], in_1, in_3);
  xor xor_2 (xor_2_out[0], in_1, in_5);
  xor xor_3 (xor_3_out[0], in_1, in_7);
  xor xor_4 (xor_4_out[0], in_1, in_9);
  Adder adder_1 (.a({undriven, in_2}), .b(xor_1_out), .out(adder_1_out), .cin(in_1), .cout(adder_1_cout));
  Adder adder_2 (.a({undriven_2, in_4}), .b(xor_2_out), .out(adder_2_out), .cin(adder_1_cout), .cout(adder_2_cout));
  Adder adder_3 (.a({undriven_3, in_6}), .b(xor_3_out), .out(adder_3_out), .cin(adder_2_cout), .cout(adder_3_cout));
  Adder adder_4 (.a({undriven_4, in_8}), .b(xor_4_out), .out(adder_4_out), .cin(adder_3_cout), .cout(adder_4_cout));
  LED led_1 ();  // open: in
  LED led_2 (.in(adder_1_out[0]));
  LED led_3 (.in(adder_2_out[0]));
  LED led_4 (.in(adder_4_out[0]));
  LED led_5 (.in(adder_3_out[0]));
  // Pins of 1 and 8 bits meet at {undriven_4, in_8}
  // Pins of 1 and 8 bits meet at {undriven_3, in_6}
  // Pins of 1 and 8 bits meet at xor_3_out
  // Pins of 1 and 8 bits meet at adder_3_out
  // Pins of 1 and 8 bits meet at {undriven, in_2}
  // Pins of 1 and 8 bits meet at xor_2_out
  // Pins of 1 and 8 bits meet at adder_2_out
  // Pins of 1 and 8 bits meet at {undriven_2, in_4}
  // Pins of 1 and 8 bits meet at adder_4_out
  // Pins of 1 and 8 bits meet at xor_4_out
  // Pins of 1 and 8 bits meet at adder_1_out
  // Pins of 1 and 8 bits meet at xor_1_out
endmodule
