// Logisim project AND Logic gate.circ as structural Verilog: 1 circuit, main circuit main
module main (
  input  in_1,
  input  in_2
);

  wire and_1_out;

  and and_1 (and_1_out, in_1, in_1, in_2, in_2);
  LED led_1 (.in(and_1_out));

  // Notes on the sheet:
  //   AND Gate
endmodule
