// Logisim project Shift Left Registor.circ as structural Verilog: 1 circuit, main circuit main
module main (
  input  IN,
  input  Reset,
  output out_3
);

  wire clock_1_out, d_ff_2_q, d_ff_3_q, d_ff_4_q;

  Clock clock_1 (.out(clock_1_out));
  D_Flip_Flop d_ff_1 (.clk(clock_1_out), .D(d_ff_2_q), .Q(out_3), .reset(Reset));  // open: Qn, preset, en
  D_Flip_Flop d_ff_2 (.clk(clock_1_out), .D(d_ff_3_q), .Q(d_ff_2_q), .reset(Reset));  // open: Qn, preset, en
  D_Flip_Flop d_ff_3 (.clk(clock_1_out), .D(d_ff_4_q), .Q(d_ff_3_q), .reset(Reset));  // open: Qn, preset, en
  D_Flip_Flop d_ff_4 (.clk(clock_1_out), .D(IN), .Q(d_ff_4_q), .reset(Reset));  // open: Qn, preset, en

  // Notes on the sheet:
  //   Shift Left Registor
endmodule
