// Logisim project OR Logic gate.circ as structural Verilog: 1 circuit, main circuit main
module main (
  input  in_1,
  input  OR_Gate
);

  wire or_1_out;

  or or_1 (or_1_out, in_1, in_1, OR_Gate, OR_Gate);
  LED led_1 (.in(or_1_out));
endmodule
