// Logisim project Asynchronous Counter.circ as structural Verilog: 1 circuit, main circuit main
module main (
  input  Input,
  input  Reset
);

  wire clock_1_out, j_k_ff_1_q, j_k_ff_1_qn, j_k_ff_2_q, j_k_ff_2_qn, j_k_ff_3_q, j_k_ff_3_qn, j_k_ff_4_q;

  Clock clock_1 (.out(clock_1_out));
  LED led_1 (.in(j_k_ff_1_q));
  J_K_Flip_Flop j_k_ff_1 (
    .J(Input), .clk(clock_1_out), .K(Input), .Q(j_k_ff_1_q), .Qn(j_k_ff_1_qn), .reset(Reset));  // open: preset, en
  LED led_2 (.in(j_k_ff_2_q));
  J_K_Flip_Flop j_k_ff_2 (
    .J(Input), .clk(j_k_ff_1_qn), .K(Input), .Q(j_k_ff_2_q), .Qn(j_k_ff_2_qn), .reset(Reset));  // open: preset, en
  LED led_3 (.in(j_k_ff_3_q));
  J_K_Flip_Flop j_k_ff_3 (
    .J(Input), .clk(j_k_ff_2_qn), .K(Input), .Q(j_k_ff_3_q), .Qn(j_k_ff_3_qn), .reset(Reset));  // open: preset, en
  LED led_4 (.in(j_k_ff_4_q));
  J_K_Flip_Flop j_k_ff_4 (
    .J(Input), .clk(j_k_ff_3_qn), .K(Input), .Q(j_k_ff_4_q), .reset(Reset));  // open: Qn, preset, en

  // Notes on the sheet:
  //   Clock
  //   4 Bit Asynchronous (Ripple) Counter
endmodule
