// Logisim project Encoder.circ as structural Verilog: 1 circuit, main circuit main
module main (
  input  y1,
  input  y2,
  input  y3,
  input  y4,
  input  y5,
  input  y6,
  input  y7
);

  wire or_1_out, or_2_out, or_3_out;

  or or_1 (or_1_out, y7, y6, y5, y4);
  or or_2 (or_2_out, y7, y6, y3, y2);
  or or_3 (or_3_out, y7, y5, y3, y1);
  LED led_1 (.in(or_1_out));
  LED led_2 (.in(or_2_out));
  LED led_3 (.in(or_3_out));

  // Notes on the sheet:
  //   Encoder
  //   A2
  //   A!
  //   A0
endmodule
