// Logisim project 4 Bit Registor File.circ as structural Verilog: 2 circuits, main circuit 4 Bit Registor File
module Mian (
  input  [1:0] in_1,
  input  [1:0] in_2,
  input  [3:0] in_3,
  input  [1:0] in_4,
  input  in_5,
  output [3:0] out_6,
  output [3:0] out_7
);

  wire n4_bit_registor_file_1_p6;

  // _4_Bit_Registor_File 4_bit_registor_file_1: pin names not known; wires that end beside it: in_1, in_2, in_3, in_4, in_5, n4_bit_registor_file_1_p6, out_6, out_7
  Clock clock_1 (.out(n4_bit_registor_file_1_p6));
endmodule

module _4_Bit_Registor_File (
  input  [1:0] Write_Registor,
  input  Input,
  input  [1:0] Read_Registor_1,
  input  [1:0] Read_Registor_2,
  input  [3:0] Write_Data,
  output [3:0] Read_Data_1,
  output [3:0] Read_Data_2
);

  wire and_1_out, and_2_out, and_3_out, and_4_out, clock_1_out, decoder_1_out0, decoder_1_out1,
       decoder_1_out2, decoder_1_out3;
  wire [3:0] register_1_q, register_2_q, register_3_q, register_4_q;

  Decoder #(.select(2)) decoder_1 (
    .out0(decoder_1_out0), .out1(decoder_1_out1), .out2(decoder_1_out2), .out3(decoder_1_out3),
    .sel(Write_Registor));  // open: en
  Clock clock_1 (.out(clock_1_out));
  and and_1 (and_1_out, decoder_1_out1, Input);
  and and_2 (and_2_out, decoder_1_out3, Input);
  Register #(.width(4)) register_1 (.D(Write_Data), .Q(register_1_q), .clk(clock_1_out), .clr(and_1_out));  // open: en
  Register #(.width(4)) register_2 (.D(Write_Data), .Q(register_2_q), .clk(clock_1_out), .clr(and_2_out));  // open: en
  and and_3 (and_3_out, decoder_1_out0, Input);
  and and_4 (and_4_out, decoder_1_out2, Input);
  Register #(.width(4)) register_3 (.D(Write_Data), .Q(register_3_q), .clk(clock_1_out), .clr(and_3_out));  // open: en
  Register #(.width(4)) register_4 (.D(Write_Data), .Q(register_4_q), .clk(clock_1_out), .clr(and_4_out));  // open: en
  Multiplexer #(.select(2), .width(4)) multiplexer_1 (
    .in0(register_1_q), .in1(register_3_q), .in2(register_2_q), .in3(register_4_q), .out(Read_Data_1),
    .sel(Read_Registor_1));  // open: en
  Multiplexer #(.select(2), .width(4)) multiplexer_2 (
    .in0(register_1_q), .in1(register_3_q), .in2(register_2_q), .in3(register_4_q), .out(Read_Data_2),
    .sel(Read_Registor_2));  // open: en
endmodule
