// Logisim project D Flip Flop.circ as structural Verilog: 1 circuit, main circuit main
module main (
  input  D,
  input  CLK
);

  wire and_1_out, and_2_out, and_3_out, and_4_out, not_1_out, not_2_out, not_3_out, not_4_out, not_5_out;

  not not_1 (not_1_out, D);
  not not_2 (not_2_out, and_1_out);
  and and_1 (and_1_out, D, CLK);
  not not_3 (not_3_out, and_2_out);
  and and_2 (and_2_out, not_1_out, CLK);
  and and_3 (and_3_out, not_2_out, not_5_out);
  and and_4 (and_4_out, not_4_out, not_3_out);
  not not_4 (not_4_out, and_3_out);
  not not_5 (not_5_out, and_4_out);
  LED led_1 (.in(not_4_out));
  LED led_2 (.in(not_5_out));

  // Notes on the sheet:
  //   D Flip Flop
  //   Q
  //   Q'
endmodule
