// Logisim project NOT Logic gate.circ as structural Verilog: 1 circuit, main circuit main
module main (
  input  in_1
);

  wire not_1_out;

  not not_1 (not_1_out, in_1);
  LED led_1 (.in(not_1_out));

  // Notes on the sheet:
  //   NOT Gate
endmodule
