// Logisim project NAND Logic gate.circ as structural Verilog: 1 circuit, main circuit main
module main (
  input  in_1,
  input  NAND_Gate
);

  wire and_1_out, not_1_out;

  and and_1 (and_1_out, in_1, in_1, NAND_Gate);
  LED led_1 (.in(not_1_out));
  not not_1 (not_1_out, and_1_out);
endmodule
