// Logisim project NOR Logic gate.circ as structural Verilog: 1 circuit, main circuit main
module main (
  input  in_1,
  input  in_2
);

  wire not_1_out, or_1_out;

  or or_1 (or_1_out, in_1, in_2);
  LED led_1 (.in(not_1_out));
  not not_1 (not_1_out, or_1_out);

  // Notes on the sheet:
  //   NOR Gate
endmodule
